// Logisim project CompArcTermProject_V10.circ as structural Verilog: 7 circuits, main circuit MAIN
module MAIN (
  output out_1,
  output out_2,
  output out_3,
  output out_4
);

  wire clock_1_out;
  wire [2:0] cmu_1_core0_control, cmu_1_core1_control;
  wire [15:0] cmu_1_adress_out_core0, cmu_1_adress_out_core1, cmu_1_data_out_core0, cmu_1_data_out_core1,
       core_1_adress, core_1_ddout, core_2_adress, core_2_ddout;
  wire [24:0] rom_1_data, rom_2_data;

  Clock clock_1 (.out(clock_1_out));
  CORE core_1 (
    .DATAIN(cmu_1_data_out_core0), .ADRESS(core_1_adress), .CLOCK(clock_1_out), .DDIN(core_2_ddout),
    .DDOUT(core_1_ddout), .out_6(out_1), .out_7(out_2), .Control(cmu_1_core0_control));
  CORE core_2 (
    .DATAIN(cmu_1_data_out_core1), .ADRESS(core_2_adress), .CLOCK(clock_1_out), .DDIN(core_1_ddout),
    .DDOUT(core_2_ddout), .out_6(out_3), .out_7(out_4), .Control(cmu_1_core1_control));
  CMU cmu_1 (
    .ADRESS_IN_CORE0(core_1_adress), .ADRESS_IN_CORE1(core_2_adress), .DATA_IN_CORE0(rom_1_data),
    .DATA_IN_CORE1(rom_2_data), .ADRESS_OUT_CORE0(cmu_1_adress_out_core0),
    .ADRESS_OUT_CORE1(cmu_1_adress_out_core1), .DATA_OUT_CORE0(cmu_1_data_out_core0),
    .DATA_OUT_CORE1(cmu_1_data_out_core1), .CORE1_CONTROL(cmu_1_core1_control),
    .CORE0_CONTROL(cmu_1_core0_control));
  ROM #(.addrWidth(16), .dataWidth(25)) rom_1 (.addr(cmu_1_adress_out_core0), .data(rom_1_data), .sel(1'b1));
  ROM #(.addrWidth(16), .dataWidth(25)) rom_2 (.addr(cmu_1_adress_out_core1), .data(rom_2_data), .sel(1'b1));
endmodule

module ALU (
  input  [15:0] ACC,
  input  [15:0] x,
  input  [3:0] in_3,
  input  [3:0] ALUSel,
  output OverFlow,
  output CoutADD,
  output [15:0] out_7
);

  wire adder_1_cout;
  wire [14:0] adder_1_out;
  wire [15:0] and_1_out, divider_1_out, multiplier_1_out, negator_1_out, not_1_out, or_1_out, shifter_1_out,
       shifter_2_out, subtractor_1_out, xor_1_out;
  wire [15:15] adder_2_out;

  Subtractor #(.width(16)) subtractor_1 (.a(ACC), .b(x), .out(subtractor_1_out));  // open: bin, bout
  Multiplier #(.width(16)) multiplier_1 (.a(ACC), .b(x), .out(multiplier_1_out));  // open: cin, cout
  Divider #(.width(16)) divider_1 (.a(ACC), .b(x), .out(divider_1_out));  // open: upper, rem
  Negator #(.width(16)) negator_1 (.in(ACC), .out(negator_1_out));
  Shifter #(.width(16)) shifter_1 (.in(ACC), .\dist (in_3), .out(shifter_1_out));
  Shifter #(.width(16), .shift("lr")) shifter_2 (.in(ACC), .\dist (in_3), .out(shifter_2_out));
  assign and_1_out = ACC & x;  // AND_Gate and_1, 16 bits wide
  assign xor_1_out = ACC ^ x;  // XOR_Gate xor_1, 16 bits wide
  assign or_1_out = ACC | x;  // OR_Gate or_1, 16 bits wide
  assign not_1_out = ~ACC;  // NOT_Gate not_1, 16 bits wide
  Adder #(.width(15)) adder_1 (.a(ACC[14:0]), .b(x[14:0]), .out(adder_1_out), .cout(adder_1_cout));  // open: cin
  Adder #(.width(1)) adder_2 (.a(ACC[15]), .b(x[15]), .out(adder_2_out[15]), .cin(adder_1_cout), .cout(CoutADD));
  xor xor_2 (OverFlow, adder_1_cout, CoutADD);
  Multiplexer #(.select(4), .width(16), .enable("false")) multiplexer_1 (
    .in0({adder_2_out[15], adder_1_out}), .in1(subtractor_1_out), .in2(multiplier_1_out),
    .in3(divider_1_out), .in4(negator_1_out), .in5(shifter_1_out), .in6(shifter_2_out), .in7(and_1_out),
    .in8(xor_1_out), .in9(or_1_out), .in10(not_1_out), .out(out_7), .sel(ALUSel));  // open: in11, in12, in13, in14, in15
endmodule

module Cashe (
  input  [15:0] Data_In,
  input  [15:0] Address
);

  wire clock_1_out, comparator_1_eq, comparator_2_eq, comparator_3_eq, comparator_4_eq, comparator_5_eq,
       comparator_6_eq, comparator_7_eq, comparator_8_eq, comparator_9_lt, comparator_10_lt,
       comparator_11_lt, comparator_12_eq, comparator_13_eq, comparator_14_eq, comparator_15_eq, or_1_out,
       or_2_out, or_3_out, or_4_out;
  wire [1:0] counter_1_q;
  wire [15:0] counter_2_q, counter_3_q, counter_4_q, counter_5_q, demultiplexer_1_out0, demultiplexer_1_out1,
       demultiplexer_1_out2, demultiplexer_1_out3, demultiplexer_2_out0, demultiplexer_2_out1,
       demultiplexer_2_out2, demultiplexer_2_out3, multiplexer_1_out, multiplexer_2_out, multiplexer_3_out,
       register_1_q, register_2_q, register_3_q, register_4_q, register_5_q, register_6_q, register_7_q,
       register_8_q;

  Clock clock_1 (.out(clock_1_out));
  Counter #(.width(2), .max('h3)) counter_1 (.Q(counter_1_q), .clk(clock_1_out));  // open: load, D, count, carry, clr
  Demultiplexer #(.select(2), .width(16), .enable("false")) demultiplexer_1 (
    .out0(demultiplexer_1_out0), .out1(demultiplexer_1_out1), .out2(demultiplexer_1_out2),
    .out3(demultiplexer_1_out3), .in(Address), .sel(counter_1_q));
  Register #(.width(16)) register_1 (
    .D(demultiplexer_1_out0), .en(or_1_out), .Q(register_1_q), .clk(clock_1_out));  // open: clr
  or or_1 (or_1_out, comparator_12_eq, comparator_1_eq);
  Register #(.width(16)) register_2 (
    .D(demultiplexer_1_out1), .en(or_2_out), .Q(register_2_q), .clk(clock_1_out));  // open: clr
  Register #(.width(16)) register_3 (
    .D(demultiplexer_1_out2), .en(or_3_out), .Q(register_3_q), .clk(clock_1_out));  // open: clr
  Register #(.width(16)) register_4 (
    .D(demultiplexer_1_out3), .en(or_4_out), .Q(register_4_q), .clk(clock_1_out));  // open: clr
  Comparator #(.width(16)) comparator_1 (.a(register_1_q), .b({16{1'b0}}), .eq(comparator_1_eq));  // open: gt, lt
  or or_2 (or_2_out, comparator_13_eq, comparator_2_eq);
  Comparator #(.width(16)) comparator_2 (.a(register_2_q), .b({16{1'b0}}), .eq(comparator_2_eq));  // open: gt, lt
  or or_3 (or_3_out, comparator_14_eq, comparator_3_eq);
  Comparator #(.width(16)) comparator_3 (.a(register_3_q), .b({16{1'b0}}), .eq(comparator_3_eq));  // open: gt, lt
  or or_4 (or_4_out, comparator_15_eq, comparator_4_eq);
  Comparator #(.width(16)) comparator_4 (.a(register_4_q), .b({16{1'b0}}), .eq(comparator_4_eq));  // open: gt, lt
  Demultiplexer #(.select(2), .width(16), .enable("false")) demultiplexer_2 (
    .out0(demultiplexer_2_out0), .out1(demultiplexer_2_out1), .out2(demultiplexer_2_out2),
    .out3(demultiplexer_2_out3), .in(Data_In), .sel(counter_1_q));
  Register #(.width(16)) register_5 (
    .D(demultiplexer_2_out0), .en(comparator_1_eq), .Q(register_5_q), .clk(clock_1_out));  // open: clr
  Register #(.width(16)) register_6 (
    .D(demultiplexer_2_out1), .en(comparator_2_eq), .Q(register_6_q), .clk(clock_1_out));  // open: clr
  Register #(.width(16)) register_7 (
    .D(demultiplexer_2_out2), .en(comparator_3_eq), .Q(register_7_q), .clk(clock_1_out));  // open: clr
  Register #(.width(16)) register_8 (
    .D(demultiplexer_2_out3), .en(comparator_4_eq), .Q(register_8_q), .clk(clock_1_out));  // open: clr
  Comparator #(.width(16)) comparator_5 (.a(register_5_q), .b(Data_In), .eq(comparator_5_eq));  // open: gt, lt
  Comparator #(.width(16)) comparator_6 (.a(register_6_q), .b(Data_In), .eq(comparator_6_eq));  // open: gt, lt
  Comparator #(.width(16)) comparator_7 (.a(register_7_q), .b(Data_In), .eq(comparator_7_eq));  // open: gt, lt
  Comparator #(.width(16)) comparator_8 (.a(register_8_q), .b(Data_In), .eq(comparator_8_eq));  // open: gt, lt
  Counter #(.width(16), .max('hffff)) counter_2 (
    .count(comparator_5_eq), .Q(counter_2_q), .clk(clock_1_out));  // open: load, D, carry, clr
  Counter #(.width(16), .max('hffff)) counter_3 (
    .count(comparator_6_eq), .Q(counter_3_q), .clk(clock_1_out));  // open: load, D, carry, clr
  Counter #(.width(16), .max('hffff)) counter_4 (
    .count(comparator_7_eq), .Q(counter_4_q), .clk(clock_1_out));  // open: load, D, carry, clr
  Counter #(.width(16), .max('hffff)) counter_5 (
    .count(comparator_8_eq), .Q(counter_5_q), .clk(clock_1_out));  // open: load, D, carry, clr
  Comparator #(.width(16)) comparator_9 (.a(counter_2_q), .b(counter_3_q), .lt(comparator_9_lt));  // open: gt, eq
  Comparator #(.width(16)) comparator_10 (.a(counter_4_q), .b(counter_5_q), .lt(comparator_10_lt));  // open: gt, eq
  Multiplexer #(.width(16), .enable("false")) multiplexer_1 (
    .in0(counter_3_q), .in1(counter_2_q), .out(multiplexer_1_out), .sel(comparator_9_lt));
  Multiplexer #(.width(16), .enable("false")) multiplexer_2 (
    .in0(counter_5_q), .in1(counter_4_q), .out(multiplexer_2_out), .sel(comparator_10_lt));
  Comparator #(.width(16)) comparator_11 (
    .a(multiplexer_1_out), .b(multiplexer_2_out), .lt(comparator_11_lt));  // open: gt, eq
  Multiplexer #(.width(16), .enable("false")) multiplexer_3 (
    .in0(multiplexer_2_out), .in1(multiplexer_1_out), .out(multiplexer_3_out), .sel(comparator_11_lt));
  Comparator #(.width(16)) comparator_12 (
    .a(counter_2_q), .b(multiplexer_3_out), .eq(comparator_12_eq));  // open: gt, lt
  Comparator #(.width(16)) comparator_13 (
    .a(counter_3_q), .b(multiplexer_3_out), .eq(comparator_13_eq));  // open: gt, lt
  Comparator #(.width(16)) comparator_14 (
    .a(counter_4_q), .b(multiplexer_3_out), .eq(comparator_14_eq));  // open: gt, lt
  Comparator #(.width(16)) comparator_15 (
    .a(counter_5_q), .b(multiplexer_3_out), .eq(comparator_15_eq));  // open: gt, lt
endmodule

module CLU (
  input  [3:0] OP,
  output [3:0] ALU_SELECT,
  output [1:0] ACC_MUX,
  output ACCSEL,
  output BRANCHSEL,
  output STORE,
  output LOAD
);

  wire and_1_out, and_2_out, and_3_out, and_4_out, and_5_out, and_6_out, and_7_out, and_8_out, and_9_out,
       and_10_out, and_11_out, and_12_out, and_13_out, and_14_out, and_18_out, and_19_out, and_20_out,
       and_21_out, not_1_out, not_2_out, not_3_out, not_4_out, not_5_out, not_6_out, not_7_out, not_8_out,
       not_9_out, not_10_out, not_11_out, not_12_out, not_13_out, not_14_out, not_15_out, not_16_out,
       not_17_out, not_18_out, not_19_out, not_20_out, not_21_out, not_22_out, not_23_out, not_24_out,
       not_25_out, not_26_out;

  not not_1 (not_1_out, OP[1]);
  not not_2 (not_2_out, OP[2]);
  not not_3 (not_3_out, OP[0]);
  not not_4 (not_4_out, OP[3]);
  not not_5 (not_5_out, OP[2]);
  not not_6 (not_6_out, OP[1]);
  not not_7 (not_7_out, OP[0]);
  not not_8 (not_8_out, OP[2]);
  not not_9 (not_9_out, OP[1]);
  not not_10 (not_10_out, OP[0]);
  not not_11 (not_11_out, OP[0]);
  not not_12 (not_12_out, OP[2]);
  not not_13 (not_13_out, OP[0]);
  and and_1 (and_1_out, OP[2], OP[0]);
  and and_2 (and_2_out, OP[2], OP[1]);
  not not_14 (not_14_out, OP[3]);
  not not_15 (not_15_out, OP[2]);
  not not_16 (not_16_out, OP[0]);
  not not_17 (not_17_out, OP[3]);
  not not_18 (not_18_out, OP[1]);
  not not_19 (not_19_out, OP[0]);
  or or_1 (BRANCHSEL, OP[1], OP[2], OP[3]);
  not not_20 (not_20_out, OP[3]);
  not not_21 (not_21_out, OP[1]);
  not not_22 (not_22_out, OP[0]);
  not not_23 (not_23_out, OP[3]);
  not not_24 (not_24_out, OP[3]);
  not not_25 (not_25_out, OP[1]);
  not not_26 (not_26_out, OP[0]);
  and and_3 (and_3_out, OP[3], OP[2], not_1_out);
  and and_4 (and_4_out, OP[3], OP[2], OP[0]);
  and and_5 (and_5_out, OP[3], not_2_out, OP[0]);
  and and_6 (and_6_out, OP[3], OP[1], not_3_out);
  and and_7 (and_7_out, not_4_out, OP[2], OP[1], OP[0]);
  and and_8 (and_8_out, OP[3], not_5_out, not_6_out, not_7_out);
  and and_9 (and_9_out, OP[3], not_8_out, OP[1], OP[0]);
  and and_10 (and_10_out, OP[3], OP[2], not_9_out, OP[0]);
  and and_11 (and_11_out, OP[3], OP[2], OP[1], not_10_out);
  and and_12 (and_12_out, OP[2], OP[1], not_11_out);
  and and_13 (and_13_out, OP[3], not_12_out, not_13_out);
  and and_14 (and_14_out, OP[3], OP[2], OP[1]);
  or or_2 (ACC_MUX[1], and_1_out, and_2_out, OP[3]);
  and and_15 (ACC_MUX[0], not_14_out, not_15_out, OP[1], not_16_out);
  and and_16 (ACCSEL, not_17_out, OP[2], not_18_out, not_19_out);
  and and_17 (STORE, not_20_out, OP[2], not_21_out, not_22_out);
  and and_18 (and_18_out, not_23_out, OP[1], OP[0]);
  and and_19 (and_19_out, not_24_out, OP[2], OP[0]);
  and and_20 (and_20_out, OP[2], OP[1]);
  and and_21 (and_21_out, OP[3], not_25_out, not_26_out);
  or or_3 (ALU_SELECT[3], and_3_out, and_4_out);
  or or_4 (ALU_SELECT[2], and_5_out, and_6_out);
  or or_5 (ALU_SELECT[1], and_7_out, and_8_out, and_9_out, and_10_out, and_11_out);
  or or_6 (ALU_SELECT[0], and_12_out, and_13_out, and_14_out);
  or or_7 (LOAD, and_18_out, and_19_out, and_20_out, and_21_out);
endmodule

module CORE (
  input  [15:0] DDIN,
  input  CLOCK,
  input  [15:0] DATAIN,
  input  [2:0] Control,
  output [15:0] DDOUT,
  output out_6,
  output out_7,
  output [15:0] ADRESS
);

  wire clu_1_accsel, clu_1_branchsel, clu_1_load, clu_1_store, not_1_out, or_1_out, or_2_out;
  wire [1:0] clu_1_acc_mux;
  wire [3:0] clu_1_alu_select, controlled_buffer_1_out;
  wire [15:0] ACC_q, adder_1_out, alu_1_out_7, bit_extender_1_out, controlled_buffer_2_out,
       demultiplexer_1_out0, demultiplexer_1_out1, multiplexer_1_out, multiplexer_2_out, multiplexer_3_out;

  Multiplexer #(.width(16), .enable("false")) multiplexer_1 (
    .in0(16'h1), .in1(bit_extender_1_out), .out(multiplexer_1_out), .sel(not_1_out));
  Adder #(.width(16)) adder_1 (.a(ADRESS), .b(multiplexer_1_out), .out(adder_1_out));  // open: cin, cout
  Register #(.width(16), .trigger("falling")) PC (.D(adder_1_out), .Q(ADRESS), .clk(CLOCK));  // open: en, clr
  not not_1 (not_1_out, clu_1_branchsel);
  Multiplexer #(.width(16), .enable("false")) multiplexer_2 (
    .in0(DDIN), .in1(demultiplexer_1_out1), .out(multiplexer_2_out), .sel(Control[0]));
  assign controlled_buffer_1_out = Control[0] ? DATAIN[15:12] : 4'bz;  // Controlled_Buffer controlled_buffer_1
  or or_1 (or_1_out, Control[2], clu_1_store);
  or or_2 (or_2_out, Control[1], clu_1_load);
  assign controlled_buffer_2_out = clu_1_branchsel ? bit_extender_1_out : 16'bz;  // Controlled_Buffer controlled_buffer_2
  assign bit_extender_1_out = {{4{DATAIN[11]}}, DATAIN[11:0]};  // Bit_Extender bit_extender_1
  RAM #(.addrWidth(12), .dataWidth(16), .bus("separate")) ram_1 (
    .addr(DATAIN[11:0]), .din(multiplexer_2_out), .data(DDOUT), .str(or_1_out), .clk(CLOCK), .ld(or_2_out));  // open: sel, clr
  Multiplexer #(.select(2), .width(16), .enable("false")) multiplexer_3 (
    .in0(DDOUT), .in1(controlled_buffer_2_out), .in2(alu_1_out_7), .out(multiplexer_3_out),
    .sel(clu_1_acc_mux));  // open: in3
  CLU clu_1 (
    .OP(controlled_buffer_1_out), .ACCSEL(clu_1_accsel), .BRANCHSEL(clu_1_branchsel), .STORE(clu_1_store),
    .LOAD(clu_1_load), .ALU_SELECT(clu_1_alu_select), .ACC_MUX(clu_1_acc_mux));
  Register #(.width(16)) ACC (.D(multiplexer_3_out), .Q(ACC_q), .clk(CLOCK));  // open: en, clr
  Demultiplexer #(.width(16), .enable("false")) demultiplexer_1 (
    .out0(demultiplexer_1_out0), .out1(demultiplexer_1_out1), .in(ACC_q), .sel(clu_1_accsel));
  ALU alu_1 (
    .ACC(demultiplexer_1_out0), .x(DDOUT), .ALUSel(clu_1_alu_select), .out_7(alu_1_out_7),
    .in_3(bit_extender_1_out[3:0]), .CoutADD(out_6), .OverFlow(out_7));
endmodule

module CMU_Control (
  input  Control1,
  input  Control0,
  output OP,
  output MuxCore1_1,
  output MuxCore1_0,
  output MuxCore0_1,
  output MuxCore0_0,
  output Load1,
  output Store1,
  output Load0,
  output Store0
);

  wire not_1_out, not_2_out, not_3_out, not_4_out, not_5_out, not_6_out, not_7_out, not_8_out, not_9_out,
       not_10_out;

  not not_1 (not_1_out, Control1);
  not not_2 (not_2_out, Control0);
  not not_3 (not_3_out, Control0);
  not not_4 (not_4_out, Control1);
  not not_5 (not_5_out, Control1);
  not not_6 (not_6_out, Control0);
  not not_7 (not_7_out, Control1);
  not not_8 (not_8_out, Control0);
  not not_9 (not_9_out, Control0);
  not not_10 (not_10_out, Control1);
  and and_1 (OP, not_1_out, not_2_out);
  and and_2 (MuxCore1_1, Control1, not_3_out);
  and and_3 (MuxCore1_0, not_4_out, Control0);
  and and_4 (MuxCore0_1, not_5_out, Control0);
  and and_5 (MuxCore0_0, Control1, not_6_out);
  and and_6 (Load1, not_7_out, Control0);
  and and_7 (Store1, Control1, not_8_out);
  and and_8 (Load0, Control1, not_9_out);
  and and_9 (Store0, not_10_out, Control0);
endmodule

module CMU (
  input  [15:0] ADRESS_IN_CORE0,
  input  [15:0] ADRESS_IN_CORE1,
  input  [24:0] DATA_IN_CORE0,
  input  [24:0] DATA_IN_CORE1,
  output [15:0] ADRESS_OUT_CORE0,
  output [15:0] ADRESS_OUT_CORE1,
  output [15:0] DATA_OUT_CORE0,
  output [2:0] CORE1_CONTROL,
  output [2:0] CORE0_CONTROL,
  output [15:0] DATA_OUT_CORE1
);

  wire comparator_1_eq, comparator_2_eq, not_1_out, not_2_out;
  wire [1:0] cmu_control_1_muxcore0_0, cmu_control_1_muxcore1_0;
  wire [15:0] bit_extender_1_out, bit_extender_2_out, bit_extender_3_out, bit_extender_4_out,
       controlled_buffer_1_out, controlled_buffer_2_out;

  Comparator #(.width(1)) comparator_1 (.a(1'b1), .b(DATA_IN_CORE1[24]), .eq(comparator_1_eq));  // open: gt, lt
  not not_1 (not_1_out, comparator_1_eq);
  Comparator #(.width(1)) comparator_2 (.a(1'b1), .b(DATA_IN_CORE0[24]), .eq(comparator_2_eq));  // open: gt, lt
  assign controlled_buffer_1_out = not_2_out ? DATA_IN_CORE0[15:0] : 16'bz;  // Controlled_Buffer controlled_buffer_1
  not not_2 (not_2_out, comparator_2_eq);
  assign controlled_buffer_2_out = not_1_out ? DATA_IN_CORE1[15:0] : 16'bz;  // Controlled_Buffer controlled_buffer_2
  CMU_Control cmu_control_1 (
    .Control1(comparator_2_eq), .Control0(comparator_1_eq), .OP(CORE0_CONTROL[0]),
    .MuxCore1_1(cmu_control_1_muxcore1_0[1]), .MuxCore1_0(cmu_control_1_muxcore1_0[0]),
    .MuxCore0_1(cmu_control_1_muxcore0_0[1]), .MuxCore0_0(cmu_control_1_muxcore0_0[0]),
    .Load1(CORE1_CONTROL[1]), .Store1(CORE1_CONTROL[2]), .Load0(CORE0_CONTROL[1]), .Store0(CORE0_CONTROL[2]));
  assign bit_extender_1_out = {{4{1'b0}}, DATA_IN_CORE1[23:12]};  // Bit_Extender bit_extender_1
  assign bit_extender_2_out = {{4{1'b0}}, DATA_IN_CORE1[11:0]};  // Bit_Extender bit_extender_2
  assign bit_extender_3_out = {{4{1'b0}}, DATA_IN_CORE0[23:12]};  // Bit_Extender bit_extender_3
  assign bit_extender_4_out = {{4{1'b0}}, DATA_IN_CORE0[11:0]};  // Bit_Extender bit_extender_4
  Multiplexer #(.select(2), .width(16), .enable("false")) multiplexer_1 (
    .in0(controlled_buffer_1_out), .in1(bit_extender_3_out), .in2(bit_extender_2_out), .out(DATA_OUT_CORE0),
    .sel(cmu_control_1_muxcore0_0));  // open: in3
  Multiplexer #(.select(2), .width(16), .enable("false")) multiplexer_2 (
    .in0(controlled_buffer_2_out), .in1(bit_extender_1_out), .in2(bit_extender_4_out), .out(DATA_OUT_CORE1),
    .sel(cmu_control_1_muxcore1_0));  // open: in3

  assign ADRESS_OUT_CORE0 = ADRESS_IN_CORE0;
  assign ADRESS_OUT_CORE1 = ADRESS_IN_CORE1;
  assign CORE1_CONTROL[0] = CORE0_CONTROL[0];

  // Notes on the sheet:
  //   Y
  //   Z
  //   Y
  //   Z
  //   Normal
  //   Normal
endmodule
